# Fritzing sketch Nano_ESP8266 (saved by Fritzing 0.9.4)
breadboards: 1

parts:
  Bauteil1 = Arduino Nano (Rev3.0)
  U1 = ESP8266 WiFi Module [part_number=ESP8266]  # not connected
  R1 = Resistor [tolerance=±5% resistance=1k package="2512 [SMD]"]
  R2 = Resistor [tolerance=±5% resistance=2.2k package="0603 [SMD]"]  # not connected

nets:
  N1: Bauteil1.D2, R1.Pin_0

notes:
  3.3 V
  1 kOhm
  2.2 kOhm
  5 V
  GND

custom parts:
  ESP8266 WiFi Module: Generic WiFi Module based on the ESP8266 with onboard PCB antenna and UART communications
